// Digital circuit main.dig as structural Verilog
module main (
  input  clk
);

  wire addrspacedivider_1_isel, addrspacedivider_1_sel, addrspacedivider_2_isel, addrspacedivider_2_sel,
       addrspacedivider_3_sel, and_1_out, and_2_out, and_3_out, and_4_out, and_5_out, and_6_out, Clock,
       cpu_1_p9, delay_1_out, demultiplexer_1_out_0, demultiplexer_1_out_1, demultiplexer_1_out_2, MemE,
       MemW, pulldown_2_out, Reset, rs_ff_1_nq, rs_ff_1_q, switch_1_b;
  wire [15:0] addrspacedivider_1_addrlow, addrspacedivider_1_iaddrlow, addrspacedivider_1_nextaddrspace,
       addrspacedivider_2_addrlow, addrspacedivider_2_iaddrlow, addrspacedivider_2_nextaddrspace,
       addrspacedivider_3_addrlow, counterpreset_1_out, cpu_1_p5, multiplexer_1_out;
  wire [31:0] cpu_1_p6, cpu_1_p10, DataIn, InstructionIn, ram_1_p10, romdualport_1_d2;
  wire [31:16] cpu_1_p5_2;

  Button u_Reset (.out(Reset));
  Switch #(.poles(2)) switch_1 (.A(1'b1), .B(switch_1_b));
  Delay #(.delayTime(10)) delay_1 (.in(Reset), .out(delay_1_out));
  PullDown pulldown_1 (.out(switch_1_b));
  and and_1 (and_1_out, delay_1_out, ~switch_1_b);  // And
  PullDown pulldown_2 (.out(pulldown_2_out));
  or or_1 (Clock, and_1_out, pulldown_2_out);
  // CPU cpu_1: pin names not known; wires that end beside it: DataIn, InstructionIn, Clock, Reset, {cpu_1_p5_2, cpu_1_p5}, cpu_1_p6, MemE, MemW, cpu_1_p9, cpu_1_p10
  and and_2 (and_2_out, MemE, rs_ff_1_nq);
  AddrSpaceDivider addrspacedivider_1 (
    .HighAddrSpace({16{1'b0}}), .Addr(cpu_1_p6), .IAddr(cpu_1_p10), .MemEnable(and_2_out),
    .IEnable(rs_ff_1_nq), .AddrLow(addrspacedivider_1_addrlow), .Sel(addrspacedivider_1_sel),
    .IAddrLow(addrspacedivider_1_iaddrlow), .ISel(addrspacedivider_1_isel),
    .NextAddrSpace(addrspacedivider_1_nextaddrspace));
  and and_3 (and_3_out, addrspacedivider_1_sel, MemW);
  AddrSpaceDivider addrspacedivider_2 (
    .HighAddrSpace(multiplexer_1_out), .Addr(cpu_1_p6), .IAddr(cpu_1_p10), .MemEnable(MemE), .IEnable(1'b1),
    .AddrLow(addrspacedivider_2_addrlow), .Sel(addrspacedivider_2_sel),
    .IAddrLow(addrspacedivider_2_iaddrlow), .ISel(addrspacedivider_2_isel),
    .NextAddrSpace(addrspacedivider_2_nextaddrspace));
  AddrSpaceDivider addrspacedivider_3 (
    .HighAddrSpace(addrspacedivider_2_nextaddrspace), .Addr(cpu_1_p6), .IAddr(cpu_1_p10), .MemEnable(MemE),
    .IEnable(1'b1), .AddrLow(addrspacedivider_3_addrlow), .Sel(addrspacedivider_3_sel));  // open: IAddrLow, ISel, NextAddrSpace
  RS_FF rs_ff_1 (.S(and_3_out), .C(Clock), .R(Reset), .Q(rs_ff_1_q), .nQ(rs_ff_1_nq));
  Multiplexer #(.Bits(16)) multiplexer_1 (
    .sel(rs_ff_1_q), .in_0(addrspacedivider_1_nextaddrspace), .in_1({16{1'b0}}), .out(multiplexer_1_out));
  ROMDualPort #(.AddrBits(14), .isProgramMemory("true"), .Bits(32)) romdualport_1 (
    .A1(addrspacedivider_1_addrlow[15:2]), .s1(addrspacedivider_1_sel),
    .A2(addrspacedivider_1_iaddrlow[15:2]), .s2(addrspacedivider_1_isel), .D1(DataIn), .D2(romdualport_1_d2));
  // Ram ram_1: pin names not known; wires that end beside it: addrspacedivider_2_addrlow, {cpu_1_p5_2, cpu_1_p5}, cpu_1_p9, addrspacedivider_2_sel, MemW, addrspacedivider_2_iaddrlow, addrspacedivider_2_isel, Clock, DataIn, ram_1_p10
  Demultiplexer #(.Selector_Bits(2)) demultiplexer_1 (
    .sel(addrspacedivider_3_addrlow[1:0]), .in(addrspacedivider_3_sel), .out_0(demultiplexer_1_out_0),
    .out_1(demultiplexer_1_out_1), .out_2(demultiplexer_1_out_2));  // open: out_3
  PullDown #(.Bits(32)) pulldown_3 (.out(romdualport_1_d2));
  and and_4 (and_4_out, demultiplexer_1_out_2, MemW);
  PullDown #(.Bits(32)) pulldown_4 (.out(ram_1_p10));
  and and_5 (and_5_out, demultiplexer_1_out_1, MemW);
  Stop stop_1 (.stop(and_4_out));
  assign InstructionIn = romdualport_1_d2 | ram_1_p10;  // Or or_2, 32 bits wide
  and and_6 (and_6_out, demultiplexer_1_out_0, MemW);
  CounterPreset #(.Bits(16)) counterpreset_1 (
    .en(and_5_out), .C(Clock), .dir(1'b0), .in({16{1'b0}}), .ld(1'b0), .clr(Reset), .out(counterpreset_1_out));  // open: ovf
  Terminal terminal_1 (.D(cpu_1_p5[6:0]), .C(Clock), .en(and_6_out));
  GraphicCard #(.graphicHeight(256), .graphicWidth(256), .Bits(16)) graphiccard_1 (
    .A({1'b0, counterpreset_1_out}), .str(and_5_out), .C(Clock), .ld(1'b0), .B(1'b0), .D(cpu_1_p5));

  // Notes on the sheet:
  //   clk: Hz: 5000
  //   contents of romdualport_1 (hex, n*v repeats v):
  //   20f21,5ef10,a4fa2,820,18a0,a30900,e12c36,812080,14fa2,811800,812880
  //   ,fffe8022,22,107ef10,21e035,23e235,25e435,3fe635,801800,108a1
  //   ,fb011897,920,a0a0,3c32636,810080,1111a,88fa2,802800,3041090,201a1
  //   ,f8023432,451890,152910,fffd4022,201a1,a0a0,f6023832,c1ef9a,81e91a
  //   ,41e89a,1e81a,105ef10,1f01b,81f380,10221,f4c04217,2444210,2a0
  //   ,1320,a0a0,3c25036,c4035,464210,145290,806080,34fa2,801300,fffe0022
  //   ,807f80,1f01b,1a0,c41836,c41080,143190,ffff4022,801100,803080
  //   ,1f01b,321111,121191,862080,1f01b
endmodule
